# Fritzing sketch Main_unit_Sketch (saved by Fritzing 0.8.7b)
breadboards: 1

parts:
  U1 = NodeMCU V1.0
  OLED1 = SSD1306 0.96in 128x64 I2C Monochrome OLED Display
  Part1 = SRF05 Ultrasonic Rangefinder
  M1 = 4 way omron relay module
  LED1 = LED - 5mm [color="Yellow (595nm)" package="5 mm [THT]"]
  LED2 = LED - 5mm [color="Red (633nm)" package="5 mm [THT]"]
  LED3 = LED - 5mm [color="Orange (612nm)" package="5 mm [THT]"]
  R1 = Resistor [tolerance=±5% resistance=220 package=THT]
  R2 = Resistor [tolerance=±5% resistance=220 package=THT]
  R3 = Resistor [tolerance=±5% resistance=220 package=THT]
  J1 = Piezo Speaker
  VCC1 = Battery block 9V

nets:
  N1: U1.D1, OLED1.SCL
  N2: U1.D2, OLED1.SDA
  N3: U1.D3, M1.CH1, R1.Pin_0
  N4: U1.D4, M1.CH2, R2.Pin_0
  N5: U1.D5, M1.CH3, R3.Pin_0
  N6: U1.D6, Part1.Trig
  N7: U1.D7, Part1.Echo
  N8: U1.D8, J1.pin2
  GND: OLED1.GND, Part1.GND, M1.DC-, LED1.cathode, LED2.cathode, LED3.cathode, J1.pin1, VCC1.-
  VCC: OLED1.VCC, Part1.VCC, M1.DC+, VCC1.+
  N9: LED1.anode, R3.Pin_1
  N10: LED2.anode, R2.Pin_1
  N11: LED3.anode, R1.Pin_1

custom parts:
  NodeMCU V1.0: ESP8266 based NodeMCU
  4 way omron relay module: Low Level 5V 4 Channel Solid State Relay Module SSR G3MB-202P 240V 2A Output with Resistive Fuse.
