# Fritzing sketch Smart_AC_controller_Sketch (saved by Fritzing 0.8.7b)
breadboards: 1

parts:
  PIR1 = PIR sensor
  Part1 = Adafruit BME680 [part_number="Adafruit #3660"]
  R1 = Photocell (LDR) [package=THT]
  OLED1 = SSD1306 0.96in 128x64 I2C Monochrome OLED Display
  KY-1 = Keyes Relay [package=THT]
  U1 = NodeMCU V1.0
  U2 = TRIAC [package=sot223]
  U3 = MOC3031-M [package=dil06]
  R3 = Resistor [tolerance=±5% resistance=220 package=THT]
  KY-2 = Keyes Relay [package=THT]
  M1 = DC Motor
  R2 = Resistor [tolerance=±5% resistance=220 package=THT]
  J1 = Piezo Speaker

nets:
  VCC: PIR1.VDD, Part1.VCC, R1.pin_0, OLED1.VCC, KY-1.power, U1.3V3, KY-2.power
  N1: PIR1.SIG, U1.D3
  GND: PIR1.GND, Part1.GND, OLED1.GND, KY-1.ground, U1.GND, U3.2, R3.Pin_0, KY-2.ground, J1.pin1
  N2: Part1.SDI/SDA, OLED1.SDA, U1.D2
  N3: Part1.SCK/SCL, OLED1.SCL, U1.D1
  N4: R1.pin_1, U1.D8, R3.Pin_1
  N5: KY-1.signal, U1.D4
  N6: U1.D5, U3.1
  N7: U1.D6, KY-2.signal
  N8: U1.D7, J1.pin2
  N9: U2.M1, R2.Pin_1
  N10: U2.M2, M1.pin_1
  N11: U2.G, U3.6
  N12: U3.4, R2.Pin_0

notes:
  Humidifier Relay
  Lights Relay
  230v AC Volts IN

custom parts:
  Keyes Relay: The Keyes 5V relay module is suitable for SCM development, home appliance control. It uses a 5V~12V TIL control signal which can control DC / AC signal.
  NodeMCU V1.0: ESP8266 based NodeMCU
