# Fritzing sketch Sub_unit_Sketch (saved by Fritzing 0.8.7b)
breadboards: 1

parts:
  U1 = NodeMCU V1.0
  PIR1 = PIR sensor
  R1 = Photocell (LDR) [package=THT]
  DHT1 = DHT11 Humitidy and Temperature Sensor
  Part1 = MQ-9 breakout
  Q1 = NPN-Transistor [package="TO92 [THT]"]
  R2 = Resistor [tolerance=±5% resistance=220 package=THT]
  R3 = Resistor [tolerance=±5% resistance=220 package=THT]
  VCC1 = 4 x AAA Battery Mount

nets:
  N1: U1.D4, DHT1.DATA, R3.Pin_0
  N2: U1.GND, PIR1.SIG
  N3: U1.D5, Q1.E
  N4: U1.A0, Part1.AO
  VDD: PIR1.VDD, R1.pin_1, DHT1.VDD, Part1.VCC, Q1.C, R3.Pin_1, VCC1.+
  GND: PIR1.GND, DHT1.GND, Part1.GND, R2.Pin_1, VCC1.-
  N5: R1.pin_0, Q1.B, R2.Pin_0

custom parts:
  NodeMCU V1.0: ESP8266 based NodeMCU
  DHT11 Humitidy and Temperature Sensor: DHT11 Humidity and Temperature Sensor
  MQ-9 breakout: SKU: 101284
